// Logisim project playground.circ as structural Verilog: 1 circuit, main circuit main
module main (
  input  in_1,
  input  in_2,
  input  in_3,
  input  in_4,
  input  in_5,
  input  in_6,
  input  in_7,
  input  in_8,
  input  in_9,
  input  in_10,
  input  in_11,
  input  in_12,
  input  in_13,
  input  in_14,
  input  in_15,
  input  in_16,
  input  in_17,
  input  in_18,
  input  in_19,
  input  in_20,
  input  in_21,
  input  in_22,
  input  in_23,
  input  in_24,
  input  in_25,
  input  in_26,
  input  in_27,
  input  in_28,
  input  in_29,
  input  in_30,
  input  in_31,
  input  in_32,
  output out_33
);

  wire and_1_out, and_2_out, and_3_out, and_4_out, and_5_out, and_6_out, and_7_out, demultiplexer_1_out0,
       demultiplexer_1_out1, demultiplexer_2_out0, demultiplexer_2_out1, demultiplexer_3_out0,
       demultiplexer_3_out1, demultiplexer_4_out0, demultiplexer_4_out1, demultiplexer_5_out0,
       demultiplexer_5_out1, multiplexer_1_out, multiplexer_2_out, multiplexer_5_out, nand_1_out, nand_2_out,
       nand_3_out, not_1_out, not_2_out, not_3_out, not_4_out, not_5_out, not_6_out, not_7_out, not_8_out,
       not_9_out, not_10_out, or_1_out, or_2_out, or_3_out, or_4_out;

  Multiplexer multiplexer_1 (.in0(in_7), .in1(in_9), .out(multiplexer_1_out), .sel(in_15));  // open: en
  Multiplexer multiplexer_2 (.in0(in_10), .in1(in_13), .out(multiplexer_2_out), .sel(in_15));  // open: en
  Multiplexer multiplexer_3 (.in0(in_17), .in1(in_18), .sel(in_22));  // open: out, en
  Multiplexer multiplexer_4 (.in0(in_20), .in1(in_21), .sel(in_23));  // open: out, en
  not not_1 (not_1_out, in_27);
  not not_2 (not_2_out, in_4);
  Multiplexer multiplexer_5 (
    .in0(multiplexer_1_out), .in1(multiplexer_2_out), .out(multiplexer_5_out), .sel(in_14));  // open: en
  and and_1 (and_1_out, in_25, not_1_out);
  and and_2 (and_2_out, in_25, in_27, in_27);
  and and_3 (and_3_out, in_1, not_2_out);
  and and_4 (and_4_out, in_2, in_4);
  or or_1 (or_1_out, and_3_out, and_3_out, and_4_out);
  not not_3 (not_3_out, in_6);
  not not_4 (not_4_out, in_11);
  not not_5 (not_5_out, in_31);
  or or_2 (or_2_out, not_3_out, not_4_out, not_4_out);
  nand nand_1 (nand_1_out, in_16, in_16, in_16, in_16);
  nand nand_2 (nand_2_out, in_19, in_19, in_19);
  Demultiplexer demultiplexer_1 (
    .out0(demultiplexer_1_out0), .out1(demultiplexer_1_out1), .in(and_5_out), .sel(in_29));  // open: en
  and and_5 (and_5_out, in_26, not_5_out);
  Demultiplexer demultiplexer_2 (
    .out0(demultiplexer_2_out0), .out1(demultiplexer_2_out1), .in(and_6_out), .sel(in_29));  // open: en
  and and_6 (and_6_out, in_26, in_31);
  not not_6 (not_6_out, in_3);
  not not_7 (not_7_out, in_5);
  nand nand_3 (nand_3_out, nand_2_out, in_24, in_24);
  or or_3 (or_3_out, not_6_out, not_6_out, not_6_out, not_7_out);
  not not_8 (not_8_out, or_3_out);
  // NAND_Gate nand_4 is placed but not wired
  // NOT_Gate not_9 has open pins: in=open, out=not_9_out
  or or_4 (or_4_out, in_8, in_12);
  not not_10 (not_10_out, and_7_out);
  and and_7 (and_7_out, in_12, in_12, in_8);
  Demultiplexer demultiplexer_3 (
    .out0(demultiplexer_3_out0), .out1(demultiplexer_3_out1), .in(demultiplexer_4_out0), .sel(in_30));  // open: en
  Demultiplexer demultiplexer_4 (
    .out0(demultiplexer_4_out0), .out1(demultiplexer_4_out1), .in(in_28), .sel(in_32));  // open: en
  Demultiplexer demultiplexer_5 (
    .out0(demultiplexer_5_out0), .out1(demultiplexer_5_out1), .in(demultiplexer_4_out1), .sel(in_30));  // open: en
  // NAND_Gate nand_5 is placed but not wired
  // AND_Gate and_8 is placed but not wired
endmodule
