// Logisim project alu.circ as structural Verilog: 1 circuit, main circuit main
module main (
  input  [15:0] in_1,
  input  [15:0] in_2,
  input  zx,
  input  nx,
  input  zy,
  input  ny,
  input  f,
  input  no,
  input  [15:0] in_9,
  input  in_10,
  input  [15:0] in_11,
  input  [15:0] in_12,
  input  [4:0] in_13,
  output [15:0] out_14,
  output [15:0] out_15
);

  wire [15:0] adder_1_out, adder_2_out, adder_3_out, and_1_out, and_2_out, and_3_out, and_4_out, and_5_out,
       bit_extender_1_out, bit_extender_2_out, bit_extender_3_out, bit_extender_4_out, bit_extender_5_out,
       bit_extender_6_out, not_1_out, not_2_out, not_3_out, or_1_out, xor_1_out, xor_2_out;

  assign bit_extender_1_out = {{15{zx}}, zx};  // Bit_Extender bit_extender_1
  assign bit_extender_2_out = {{15{nx}}, nx};  // Bit_Extender bit_extender_2
  assign bit_extender_3_out = {{15{zy}}, zy};  // Bit_Extender bit_extender_3
  assign bit_extender_4_out = {{15{ny}}, ny};  // Bit_Extender bit_extender_4
  assign not_1_out = ~in_11;  // NOT_Gate not_1, 16 bits wide
  assign not_2_out = ~in_12;  // NOT_Gate not_2, 16 bits wide
  assign and_1_out = in_1 & ~bit_extender_1_out;  // AND_Gate and_1, 16 bits wide
  assign and_2_out = in_2 & ~bit_extender_3_out;  // AND_Gate and_2, 16 bits wide
  assign bit_extender_5_out = {{15{f}}, f};  // Bit_Extender bit_extender_5
  assign not_3_out = ~in_9;  // NOT_Gate not_3, 16 bits wide
  assign bit_extender_6_out = {{15{no}}, no};  // Bit_Extender bit_extender_6
  Multiplexer #(.select(2), .width(16)) multiplexer_1 (
    .in0(in_9), .in1({16{1'b0}}), .in2(not_3_out), .in3({16{1'b1}}), .out(out_15), .en(1'b1));  // open: sel
  Adder #(.width(16)) adder_1 (.a({16{1'b1}}), .b(not_1_out), .out(adder_1_out));  // open: cin, cout
  Adder #(.width(16)) adder_2 (.a({16{1'b1}}), .b(not_2_out), .out(adder_2_out));  // open: cin, cout
  assign xor_1_out = and_1_out ^ bit_extender_2_out;  // XOR_Gate xor_1, 16 bits wide
  assign xor_2_out = and_2_out ^ bit_extender_4_out;  // XOR_Gate xor_2, 16 bits wide
  Adder #(.width(16)) adder_3 (.a(xor_1_out), .b(xor_2_out), .out(adder_3_out));  // open: cin, cout
  assign and_3_out = adder_3_out & bit_extender_5_out;  // AND_Gate and_3, 16 bits wide
  assign and_4_out = xor_1_out & xor_2_out;  // AND_Gate and_4, 16 bits wide
  assign or_1_out = and_3_out | and_5_out;  // OR_Gate or_1, 16 bits wide
  assign and_5_out = and_4_out & ~bit_extender_5_out;  // AND_Gate and_5, 16 bits wide
  Multiplexer #(.select(5), .width(18)) multiplexer_2 (.sel(in_13));  // open: in0, in1, in2, in3, in4, in5, in6, in7, in8, in9, in10, in11, in12, in13, in14, in15, in16, in17, in18, in19, in20, in21, in22, in23, in24, in25, in26, in27, in28, in29, in30, in31, out, en
  assign out_14 = or_1_out ^ bit_extender_6_out;  // XOR_Gate xor_3, 16 bits wide

  // Notes on the sheet:
  //   x
  //   y
endmodule
