// Logisim project playground.circ as structural Verilog: 1 circuit, main circuit main
module main (
  input  in_1,
  input  in_2,
  input  in_3,
  input  [15:0] in_4,
  input  [15:0] in_5,
  input  [15:0] in_6,
  output [15:0] out_7,
  output [15:0] out_8
);

  wire and_1_out, and_2_out, or_1_out, xor_1_out, xor_2_out;

  xor xor_1 (xor_1_out, in_1, in_2);
  and and_1 (and_1_out, in_1, in_2);
  xor xor_2 (xor_2_out, xor_1_out, in_3);
  and and_2 (and_2_out, xor_1_out, in_3);
  assign out_8 = in_4 & in_5;  // AND_Gate and_3, 16 bits wide
  assign out_7 = in_4 ^ in_5;  // XOR_Gate xor_3, 16 bits wide
  or or_1 (or_1_out, and_1_out, and_2_out, and_1_out);
endmodule
